# Fritzing sketch Joystick_mouse (saved by Fritzing 0.8.7b)
circuit board: 8.46667cm x 5.64444cm
breadboards: 1

parts:
  Joystick = Thumb Joystick
  Teensy_3_1 = Teensy 3.1
  Part1 = Barometric Pressure Sensor - BMP085 Breakout  # not connected

nets:
  N1: Joystick.GND, Teensy_3_1.AGND
  N2: Joystick.SEL, Teensy_3_1.D4
  N3: Joystick.HORZ, Teensy_3_1.A0/D14
  N4: Joystick.VERT, Teensy_3_1.A1/D15
  VCC: Joystick.VCC, Teensy_3_1.3V3
